# Fritzing sketch cigar_box (saved by Fritzing 0.9.3b)
perfboards: 1

parts:
  Part1 = Arduino Pro Mini v13
  J1 = Dagu DGServo 9g header connector (female) [package=THT]
  J2 = Dagu DGServo 9g header connector (female) [package=THT]  # not connected
  J3 = Dagu DGServo 9g header connector (female) [package=THT]  # not connected
  J4 = Dagu DGServo 9g header connector (female) [package=THT]  # not connected
  J5 = Dagu DGServo 9g header connector (female) [package=THT]
  BAT1 = Battery Holders [package=battery-aa]
  TP1 = TP4056 [chip_label=TP4056 package="DIP (Dual Inline) [THT]"]
  Part2 = Pololu 5V Step-Up Regulator
  TTP223B1 = TTP223B Capacitive Touch Sensor Module
  R2 = Basic Flex Resistor

nets:
  N1: Part1.GND, J5.pulse, TP1.pin6, R2.Pin_2
  VCC: Part1.VCC, J5.Vcc, Part2.VIN
  N2: Part1.D11_PWM/MOSI, J1.pulse
  N3: Part1.D10_PWM/SS, J5.gnd
  N4: Part1.D9_PWM, R2.pin_1
  N5: Part1.D2, TTP223B1.SIG
  N6: BAT1.-, TP1.pin4
  N7: BAT1.+, TP1.pin5
  N8: TP1.pin3, Part2.VOUT

custom parts:
  TP4056: A DIP stand-in part for whatever IC you want. With 6 pins on a 300mil dual inline package (DIP) footprint.
  TTP223B Capacitive Touch Sensor Module: The TTP223B capacitive touch sensor module uses the TTP223B IC. The appropriate voltage is approximately 2 to 5.5 volts.

// code stored in the sketch: cigar-box.ino
#define PIN_PLANCH 		11
#define PIN_DOOR 			10
#define PIN_TOUCH_1 	8
#define PIN_TOUCH_1 	7
#define PIN_LIGHT			9
